# Fritzing sketch full_project (saved by Fritzing 0.9.0b)
circuit board: 8.46667cm x 5.64444cm
breadboards: 1

parts:
  U1 = WT32 [package=wt32]
  Teensy_3_1 = Teensy 3.1
  SP_L = SPEAKER [package=pcb_mount_speaker]
  MIC_L = Microphone
  MIC_R = Microphone
  SP_R = SPEAKER [package=pcb_mount_speaker]
  LiPo_R = LIPO-1000mAh [package=lipo-1000]
  LiPo_L = LIPO-1000mAh [package=lipo-1000]
  LED_BLUE = smd LED [color="Blue (525nm)" package="0603 [SMD]"]
  D1 = Rectifier Diode [part_number=1N4001 package="300 mil [THT]"]
  JP1 = USB_MICROB_PLUG [package=micro-b-th]
  V_BOOST_R = IC, DIP package, 6 pins [chip_label=IC]
  LEVEL_CVTR = IC, DIP package, 14 pins [chip_label=IC]
  LED_R = SMD RGB LED (WS2812) [package=5050]
  V_BOOST_L = IC, DIP package, 6 pins [chip_label=IC]
  LED_L = SMD RGB LED (WS2812) [package=5050]
  LED_R1 = SMD RGB LED (WS2812) [package=5050]
  LED_R2 = SMD RGB LED (WS2812) [package=5050]
  LED_R3 = SMD RGB LED (WS2812) [package=5050]
  LED_R4 = SMD RGB LED (WS2812) [package=5050]
  LED_R5 = SMD RGB LED (WS2812) [package=5050]
  LED_R6 = SMD RGB LED (WS2812) [package=5050]
  LED_R7 = SMD RGB LED (WS2812) [package=5050]
  LED_R8 = SMD RGB LED (WS2812) [package=5050]
  LED_R9 = SMD RGB LED (WS2812) [package=5050]
  LED_R10 = SMD RGB LED (WS2812) [package=5050]
  LED_R11 = SMD RGB LED (WS2812) [package=5050]
  LED_L1 = SMD RGB LED (WS2812) [package=5050]
  LED_L2 = SMD RGB LED (WS2812) [package=5050]
  LED_L3 = SMD RGB LED (WS2812) [package=5050]
  LED_L4 = SMD RGB LED (WS2812) [package=5050]
  LED_L5 = SMD RGB LED (WS2812) [package=5050]
  LED_L6 = SMD RGB LED (WS2812) [package=5050]
  LED_L7 = SMD RGB LED (WS2812) [package=5050]
  LED_L8 = SMD RGB LED (WS2812) [package=5050]
  LED_L9 = SMD RGB LED (WS2812) [package=5050]
  LED_L10 = SMD RGB LED (WS2812) [package=5050]
  LED_L11 = SMD RGB LED (WS2812) [package=5050]

nets:
  GND: U1.DGND, Teensy_3_1.GND, LiPo_R.+, LiPo_L.+, LED_BLUE.cathode, D1.cathode, JP1.GND, V_BOOST_R.pin2, LEVEL_CVTR.pin7, LED_R.VSS, V_BOOST_L.pin2, LED_L.VSS, LED_R1.VSS, LED_R2.VSS, LED_R3.VSS, LED_R4.VSS, LED_R5.VSS, LED_R6.VSS, LED_R7.VSS, LED_R8.VSS, LED_R9.VSS, LED_R10.VSS, LED_R11.VSS, LED_L1.VSS, LED_L2.VSS, LED_L3.VSS, LED_L4.VSS, LED_L5.VSS, LED_L6.VSS, LED_L7.VSS, LED_L8.VSS, LED_L9.VSS, LED_L10.VSS, LED_L11.VSS
  N1: U1.USB_DN, JP1.D-
  N2: U1.USB_DP, JP1.D+
  N3: U1.RXD, Teensy_3_1.D1
  N4: U1.TXD, Teensy_3_1.D0
  N5: U1.VDDIO, Teensy_3_1.Vin, LEVEL_CVTR.pin1
  N6: U1.LED0, LED_BLUE.anode
  N7: U1.VDD_BAT, LiPo_R.-, LiPo_L.-, V_BOOST_R.pin6, V_BOOST_L.pin6
  N8: U1.VDD_CHG, JP1.VCC
  N9: U1.AGND, Teensy_3_1.AGND, D1.anode
  N10: U1.AUDIO_IN_P_RIGHT, MIC_R.pin1
  N11: U1.AUDIO_IN_N_RIGHT, MIC_R.pin2
  N12: U1.AUDIO_IN_P_LEFT, MIC_L.pin1
  N13: U1.AUDIO_IN_N_LEFT, MIC_L.pin2
  N14: U1.AUDIO_OUT_N_RIGHT, SP_R.-
  N15: U1.AUDIO_OUT_P_RIGHT, SP_R.+
  N16: U1.AUDIO_OUT_N_LEFT, SP_L.-
  N17: U1.AUDIO_OUT_P_LEFT, SP_L.+
  N18: Teensy_3_1.D5, LEVEL_CVTR.pin2
  N19: Teensy_3_1.D6, LEVEL_CVTR.pin3
  N20: V_BOOST_R.pin5, LED_R.VCC
  N21: LEVEL_CVTR.pin12, LED_L.DIn
  N22: LEVEL_CVTR.pin13, LED_R.DIn
  N23: LEVEL_CVTR.pin14, V_BOOST_L.pin5, LED_L.VCC
  N24: LED_R.DOut, LED_R1.DIn
  VDD: LED_R.VDD, LED_R1.VCC
  N25: LED_L.DOut, LED_L1.DIn
  VDD_2: LED_L.VDD, LED_L1.VCC
  N26: LED_R1.DOut, LED_R2.DIn
  VDD_3: LED_R1.VDD, LED_R2.VCC
  N27: LED_R2.DOut, LED_R3.DIn
  VDD_4: LED_R2.VDD, LED_R3.VCC
  N28: LED_R3.DOut, LED_R4.DIn
  VDD_5: LED_R3.VDD, LED_R4.VCC
  N29: LED_R4.DOut, LED_R5.DIn
  VDD_6: LED_R4.VDD, LED_R5.VCC
  N30: LED_R5.DOut, LED_R6.DIn
  VDD_7: LED_R5.VDD, LED_R6.VCC
  N31: LED_R6.DOut, LED_R7.DIn
  VDD_8: LED_R6.VDD, LED_R7.VCC
  N32: LED_R7.DOut, LED_R8.DIn
  VDD_9: LED_R7.VDD, LED_R8.VCC
  N33: LED_R8.DOut, LED_R9.DIn
  VDD_10: LED_R8.VDD, LED_R9.VCC
  N34: LED_R9.DOut, LED_R10.DIn
  VDD_11: LED_R9.VDD, LED_R10.VCC
  N35: LED_R10.DOut, LED_R11.DIn
  VDD_12: LED_R10.VDD, LED_R11.VCC
  N36: LED_L1.DOut, LED_L2.DIn
  VDD_13: LED_L1.VDD, LED_L2.VCC
  N37: LED_L2.DOut, LED_L3.DIn
  VDD_14: LED_L2.VDD, LED_L3.VCC
  N38: LED_L3.DOut, LED_L4.DIn
  VDD_15: LED_L3.VDD, LED_L4.VCC
  N39: LED_L4.DOut, LED_L5.DIn
  VDD_16: LED_L4.VDD, LED_L5.VCC
  N40: LED_L5.DOut, LED_L6.DIn
  VDD_17: LED_L5.VDD, LED_L6.VCC
  N41: LED_L6.DOut, LED_L7.DIn
  VDD_18: LED_L6.VDD, LED_L7.VCC
  N42: LED_L7.DOut, LED_L8.DIn
  VDD_19: LED_L7.VDD, LED_L8.VCC
  N43: LED_L8.DOut, LED_L9.DIn
  VDD_20: LED_L8.VDD, LED_L9.VCC
  N44: LED_L9.DOut, LED_L10.DIn
  VDD_21: LED_L9.VDD, LED_L10.VCC
  N45: LED_L10.DOut, LED_L11.DIn
  VDD_22: LED_L10.VDD, LED_L11.VCC
